# Fritzing sketch llm_2_esp32_fritz (saved by Fritzing 0.9.6b)
circuit board: 12.4661cm x 7.08967cm
breadboards: 1

parts:
  Part2 = FTDI Basic Programmer
  max98357 = male pin header, 7 pins [form="♂ (male)"]
  E1 = ESP32-Cam
  gnd_0 = male pin header, 2 pins [form="♂ (male)"]
  S3 = Pushbutton [package="[THT]"]
  10k_ohm = Pushbutton [package=THT]
  220_ohm = Pushbutton [package=THT]
  max98358 = male pin header, 4 pins [form="♂ (male)"]
  vcc = male pin header, 1 pin [form="♂ (male)"]
  1k_ohm = Pushbutton [package=THT]
  S7 = Taiway 100-SP-X-T1 SPDT Miniature Toggle Switch [part_number=100-SP-X-T1-0-0-B1-M1 package=THT]
  J1 = Camdenboss CTB0158-2 [part_number=CTB0158-2 package=THT]

nets:
  N1: Part2.RXI, E1.RX/GPIO_1
  N2: Part2.TXO, E1.TX/GPIO_3
  N3: Part2.GND, E1.GND#11, gnd_0.pin1
  N4: max98357.pin1, E1.GPIO_15
  N5: max98357.pin2, E1.GPIO_13
  N6: max98357.pin3, E1.GPIO_12
  N7: max98357.pin4, max98357.pin6, E1.GND#1, 10k_ohm.leg1, max98358.pin4, J1.pin1
  N8: max98357.pin7, E1.5V, max98358.pin3, vcc.pin1, 1k_ohm.leg1, S7.L1
  N9: E1.GPIO_14, max98358.pin1
  N10: E1.GPIO_2, max98358.pin2
  N11: E1.GPIO_4, 220_ohm.leg1
  N12: E1.GPIO_0, gnd_0.pin2
  N13: S3.Pin_1, S3.Pin_2, 1k_ohm.leg0
  N14: S3.Pin_3, 10k_ohm.leg0, 220_ohm.leg0
  N15: S7.COM, J1.pin2
